// Logisim project BCDadderCircuit.circ as structural Verilog: 1 circuit, main circuit main
module main (
  input  [3:0] A4_A3_A2_A1,
  input  [3:0] _8,
  input  in_3,
  input  in_4,
  output F4,
  output F3,
  output F2,
  output F1,
  output F5
);

  wire adder_1_cout, and_1_out, or_1_out;
  wire [3:0] adder_1_out;

  Adder #(.width(4)) adder_1 (.a(A4_A3_A2_A1), .b(_8), .out(adder_1_out), .cout(adder_1_cout));  // open: cin
  and and_1 (and_1_out, adder_1_out[3], or_1_out);
  or or_1 (or_1_out, adder_1_out[2], adder_1_out[1]);
  or or_2 (F5, and_1_out, adder_1_cout);
  Adder #(.width(4)) adder_2 (.a(adder_1_out), .b({in_3, {2{F5}}, in_4}), .out({F4, F3, F2, F1}));  // open: cin, cout

  // Notes on the sheet:
  //   7
  //   B4 B3 B2 B1
  //   4-bit Adder
  //   K
  //   S2
  //   S3
  //   S1
  //   4-bit Adder
endmodule
